# Fritzing sketch Master (saved by Fritzing 0.9.9b)

parts:
  Teensy_4_0 = Teensy 4.0
  NRF24L01 = NRF24L01+ Breakout Board
  POT2 = Rotary Potentiometer (Small) [maximum_resistance=1kΩ package=THT]
  POT1 = Rotary Potentiometer (Small) [maximum_resistance=1kΩ package=THT]
  POT0 = Rotary Potentiometer (Small) [maximum_resistance=1kΩ package=THT]
  CV1 = smd LED [color="Red (633nm)" package="0805 [SMD]"]
  CV3 = smd LED [color="Red (633nm)" package="0805 [SMD]"]
  CV2 = smd LED [color="Red (633nm)" package="0805 [SMD]"]
  MCP4728 = Adafruit MCP4728
  CV1_2 = TRRS 3.5mm Jack Breakout
  CV2_2 = TRRS 3.5mm Jack Breakout
  CV3_2 = TRRS 3.5mm Jack Breakout
  R5 = Resistor [tolerance=±5% power=0.25 resistance=100 package=THT]
  SSD1306_128x32_OLED = OLED Mono 0.56 inch blue or white  # not connected
  Reset = Pushbutton [package=THT]
  usrKey = Pushbutton [package=THT]
  bultIn_LED = smd LED [color="Blue (470nm)" package="0805 [SMD]"]
  R6 = Resistor [tolerance=±5% power=0.25 resistance=100 package=THT]

nets:
  N1: Teensy_4_0.pin_3, CV1.anode
  N2: Teensy_4_0.pin_4, CV2.anode
  N3: Teensy_4_0.pin_5, CV3.anode
  N4: Teensy_4_0.pin_11, NRF24L01.CE
  N5: Teensy_4_0.pin_12, NRF24L01.CS
  N6: Teensy_4_0.pin_13, NRF24L01.MOSI
  N7: Teensy_4_0.pin_14, NRF24L01.MISO
  N8: Teensy_4_0.pin_17, Teensy_4_0.pin_32, Reset.leg1
  N9: Teensy_4_0.pin_19, Reset.leg0
  N10: Teensy_4_0.pin_20, NRF24L01.SCK
  N11: Teensy_4_0.pin_21, bultIn_LED.cathode
  N12: Teensy_4_0.pin_22, usrKey.leg1
  N13: Teensy_4_0.pin_25, MCP4728.SDA
  N14: Teensy_4_0.pin_26, MCP4728.SCL
  N15: Teensy_4_0.pin_28, POT1.wiper
  N16: Teensy_4_0.pin_29, POT0.wiper
  N17: Teensy_4_0.pin_30, POT2.wiper
  N18: Teensy_4_0.pin_31, NRF24L01.VCC, POT2.leg2
  N19: Teensy_4_0.pin33, MCP4728.VCC
  N20: POT2.leg1, POT1.leg1, CV1_2.SLEEVE, CV3_2.SLEEVE
  N21: CV1.cathode, CV3.cathode, CV2.cathode, R5.Pin_0
  N22: MCP4728.VOUTA, CV1_2.TIP
  N23: MCP4728.VOUTB, CV2_2.TIP
  N24: MCP4728.VOUTC, CV3_2.TIP
  N25: R5.Pin_1, usrKey.leg0
  N26: bultIn_LED.anode, R6.Pin_1

custom parts:
  Teensy 4.0: The Teensy is a complete USB-based microcontoller development system, in a very small footprint, capable of implementing many types of projects. All programming is done via the USB port. No special programmer is needed, only a standard micro-USB cable and a PC or Macintosh with a USB port.
  Adafruit MCP4728: If you've ever said to yourself "Gee, I wish these four 12-bit DACs came in a single package with the ability to save their settings to an EEPROM", well I have good news. The MCP4728 is the answer to your wishes! Within it's little package, the MCP4728 has four, count em, four 12-bit DACs for whatever voltage setting needs you may have. In addition, it has the ability to store the settings for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
  OLED Mono 0.56 inch blue or white: OLED, I2C 3.3V - 5V Blue and White text versions
