# Fritzing sketch Node (saved by Fritzing 0.9.9b)

parts:
  BNO085 = Adafruit BNO085 9-DOF Orientation IMU Fusion [part_number="Addfruit #4754"]
  NRF24L01 = NRF24L01+ Breakout Board
  USB_Connector = Header 4 [package=screwterminal-3.5mm-4_lock]
  STM32F411CE = STM32F303 [package=LQFP-48]

nets:
  VCC: BNO085.VCC, USB_Connector.4, STM32F411CE.5V
  N1: BNO085.GND, USB_Connector.1, STM32F411CE.GNS
  N2: BNO085.SCL/SCK/RX, STM32F411CE.B7
  N3: BNO085.SDA/MISO/TX, BNO085.INT, STM32F411CE.B8
  GND: NRF24L01.GND, STM32F411CE.GND
  VCC_2: NRF24L01.VCC, STM32F411CE.3V3
  N4: NRF24L01.CE, STM32F411CE.B0
  N5: NRF24L01.CS, STM32F411CE.A4
  N6: NRF24L01.SCK, STM32F411CE.A5
  N7: NRF24L01.MOSI, STM32F411CE.A7
  N8: NRF24L01.MISO, STM32F411CE.A6
  N9: USB_Connector.2, STM32F411CE.A12
  N10: USB_Connector.3, STM32F411CE.A11

notes:
  STM32F411CE Blackpill - Pin Compatible

custom parts:
  STM32F303: Medium density Cortex-M3 microcontroller.
